// Logisim project mco1.circ as structural Verilog
module code128 (
  input  i1,
  input  i2,
  input  i3,
  input  i4,
  output b1,
  output b2,
  output b3,
  output b4,
  output b5,
  output b6,
  output b7,
  output b8,
  output b9,
  output b10,
  output b11
);

  wire and_1_out, and_2_out, and_3_out, and_4_out, and_5_out, and_6_out, and_7_out, and_8_out, and_9_out,
       and_10_out, and_11_out, and_12_out, and_13_out, and_14_out, and_15_out, and_16_out, and_17_out,
       and_18_out, and_19_out, and_20_out, and_21_out, and_22_out, and_23_out, and_24_out, and_25_out,
       and_26_out, and_27_out, and_28_out, and_29_out, and_30_out, not_1_out, not_2_out, not_3_out,
       not_4_out, not_5_out, not_6_out, not_7_out, not_8_out, not_9_out, not_10_out, not_11_out, not_12_out,
       not_13_out, not_14_out, not_15_out, not_16_out, not_17_out, not_18_out, not_19_out, not_20_out,
       not_21_out, not_22_out, not_23_out, not_24_out, not_25_out, not_26_out, not_27_out, not_28_out,
       not_29_out, not_30_out, not_31_out, not_32_out, not_33_out, not_34_out, not_35_out, not_36_out,
       not_37_out, not_38_out, not_39_out, not_40_out, not_41_out, not_42_out, not_43_out, not_44_out,
       not_45_out;

  not not_1 (not_1_out, i1);
  and and_1 (and_1_out, not_1_out, not_2_out, not_3_out);
  not not_2 (not_2_out, i2);
  not not_3 (not_3_out, i3);
  not not_4 (not_4_out, i2);
  and and_2 (and_2_out, not_4_out, i3, not_5_out);
  not not_5 (not_5_out, i4);
  and and_3 (and_3_out, i1, not_6_out, i4);
  not not_6 (not_6_out, i2);
  not not_7 (not_7_out, i3);
  not not_8 (not_8_out, i4);
  not not_9 (not_9_out, i1);
  and and_4 (and_4_out, not_9_out, not_10_out, not_11_out);
  not not_10 (not_10_out, i3);
  not not_11 (not_11_out, i4);
  not not_12 (not_12_out, i1);
  and and_5 (and_5_out, not_12_out, i3, i4);
  and and_6 (and_6_out, i2, not_13_out);
  not not_13 (not_13_out, i4);
  and and_7 (and_7_out, i1, i2);
  not not_14 (not_14_out, i2);
  and and_8 (and_8_out, not_14_out, not_15_out);
  not not_15 (not_15_out, i3);
  and and_9 (and_9_out, i3, not_16_out);
  not not_16 (not_16_out, i4);
  and and_10 (and_10_out, i2, i4);
  not not_17 (not_17_out, i1);
  not not_18 (not_18_out, i2);
  not not_19 (not_19_out, i3);
  not not_20 (not_20_out, i1);
  not not_21 (not_21_out, i2);
  not not_22 (not_22_out, i4);
  not not_23 (not_23_out, i2);
  not not_24 (not_24_out, i3);
  not not_25 (not_25_out, i4);
  not not_26 (not_26_out, i2);
  not not_27 (not_27_out, i1);
  not not_28 (not_28_out, i2);
  not not_29 (not_29_out, i3);
  not not_30 (not_30_out, i1);
  and and_11 (and_11_out, not_30_out, not_31_out);
  not not_31 (not_31_out, i3);
  not not_32 (not_32_out, i1);
  and and_12 (and_12_out, not_32_out, not_33_out, i4);
  not not_33 (not_33_out, i2);
  not not_34 (not_34_out, i3);
  and and_13 (and_13_out, not_34_out, i4);
  and and_14 (and_14_out, i2, not_35_out);
  not not_35 (not_35_out, i4);
  and and_15 (and_15_out, i1, i2);
  not not_36 (not_36_out, i1);
  and and_16 (and_16_out, not_36_out, not_37_out);
  not not_37 (not_37_out, i3);
  not not_38 (not_38_out, i2);
  and and_17 (and_17_out, not_38_out, not_39_out);
  not not_39 (not_39_out, i4);
  not not_40 (not_40_out, i3);
  and and_18 (and_18_out, not_40_out, not_41_out);
  not not_41 (not_41_out, i4);
  and and_19 (and_19_out, i2, i4);
  and and_20 (and_20_out, i1, i3);
  not not_42 (not_42_out, i1);
  not not_43 (not_43_out, i2);
  not not_44 (not_44_out, i4);
  not not_45 (not_45_out, i4);
  or or_1 (b2, and_1_out, and_2_out, and_3_out);
  and and_21 (and_21_out, i1, i2, not_7_out, not_8_out);
  or or_2 (b3, and_21_out, and_22_out);
  and and_22 (and_22_out, i1, i2, i3, i4);
  or or_3 (b4, and_4_out, and_5_out, and_6_out, and_7_out);
  or or_4 (b5, and_8_out, and_9_out, and_10_out);
  and and_23 (and_23_out, not_17_out, not_18_out, not_19_out, i4);
  and and_24 (and_24_out, not_20_out, not_21_out, i3, not_22_out);
  and and_25 (and_25_out, i1, not_23_out, not_24_out, not_25_out);
  and and_26 (and_26_out, i1, not_26_out, i3, i4);
  and and_27 (and_27_out, not_27_out, not_28_out, i3, i4);
  or or_5 (b7, and_27_out, and_28_out);
  and and_28 (and_28_out, i1, i2, not_29_out);
  or or_6 (b8, and_11_out, and_12_out, and_13_out, and_14_out, and_15_out);
  or or_7 (b9, and_16_out, and_17_out, and_18_out, and_19_out, and_20_out);
  and and_29 (and_29_out, not_42_out, not_43_out, i3, not_44_out);
  or or_8 (b10, and_29_out, and_30_out);
  and and_30 (and_30_out, i1, i2, i3, not_45_out);
  or or_9 (b6, and_23_out, and_24_out, and_25_out, and_26_out);
  LED led_1 (.in(b3));
  LED led_2 (.in(1'b1));
  LED led_3 (.in(b2));
  LED led_4 (.in(b6));
  LED led_5 (.in(b7));
  LED led_6 (.in(b5));
  LED led_7 (.in(b4));
  LED led_8 (.in(b8));
  LED led_9 (.in(b9));
  LED led_10 (.in(1'b0));
  LED led_11 (.in(b10));

  assign b1 = 1'b1;
  assign b11 = 1'b0;
endmodule
